# Fritzing sketch Garderner sensors prototype (saved by Fritzing 0.9.3b)
breadboards: 1

parts:
  DHT1 = DHT11 Humitidy and Temperature Sensor
  Part1 = Arduino Yun
  Part2 = Adafruit TSL2561 [part_number="Adafruit #439"]
  Part3 = Adafruit BMP180

nets:
  VDD: DHT1.VDD, Part1.5V
  N1: DHT1.DATA, Part1.D5_PWM
  GND: DHT1.GND, Part1.GND, Part2.GND, Part3.GND
  N2: Part1.D2, Part3.SDA
  N3: Part1.D3_PWM, Part3.SCL
  3V3: Part1.3V3, Part2.VIN, Part3.+5V

custom parts:
  DHT11 Humitidy and Temperature Sensor: DHT11 Humidity and Temperature Sensor
  Adafruit TSL2561: The TSL2561 luminosity sensor is an advanced digital light sensor, ideal for use in a wide range of light situations. Compared to low cost CdS cells, this sensor is more precise, allowing for exact lux calculations and can be configured for different gain/timing ranges to detect light ranges from up to 0.1 - 40,000+ Lux on the fly. The best part of this sensor is that it contains both infrared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
  Adafruit BMP180: This precision sensor from Bosch is the best low-cost sensing solution for measuring barometric pressure and temperature. Because pressure changes with altitude you can also use it as an altimeter! The sensor is soldered onto a PCB with a 3.3V regulator, I2C level shifter and pull-up resistors on the I2C pins. The BMP180 is the next-generation of sensors from Bosch, and replaces the BMP085.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
